// Logisim project Stage2.circ as structural Verilog: 3 circuits, main circuit main
module main (
);

  wire button_1_out, button_2_out, button_3_out, clock_1_out, start_1_oclk, start_1_ostartstop;
  wire [3:0] second9_1_o1;

  Button button_1 (.out(button_1_out));
  Clock clock_1 (.out(clock_1_out));
  Button button_2 (.out(button_2_out));
  Hex_Digit_Display hex_digit_display_1 ();  // open: value, dp
  Hex_Digit_Display hex_digit_display_2 ();  // open: value, dp
  Button button_3 (.out(button_3_out));
  Hex_Digit_Display hex_digit_display_3 ();  // open: value, dp
  LED led_1 (.in(start_1_ostartstop));
  Hex_Digit_Display hex_digit_display_4 (.value(second9_1_o1));  // open: dp
  Hex_Digit_Display hex_digit_display_5 ();  // open: value, dp
  Second9 second9_1 (
    .set(start_1_ostartstop), .CLK(start_1_oclk), .O1(second9_1_o1[0]), .O2(second9_1_o1[1]),
    .O3(second9_1_o1[2]), .O4(second9_1_o1[3]));
  Hex_Digit_Display hex_digit_display_6 ();  // open: value, dp
  start start_1 (
    .StartStop(button_1_out), .Split(button_2_out), .Reset(button_3_out), .CLK(clock_1_out),
    .OStartStop(start_1_ostartstop), .OCLK(start_1_oclk));  // open: OSplit, OReset
  Hex_Digit_Display hex_digit_display_7 ();  // open: value, dp
  Hex_Digit_Display hex_digit_display_8 ();  // open: value, dp

  // Notes on the sheet:
  //   Start / Stop
  //   Stopwatch Interface
  //   Split
  //   Minutes
  //   Reset
  //   Elapsed Time
  //   Seconds
  //   :
  //   Clock Started
  //   Split Time
  //   Minutes
  //   :
  //   Seconds
endmodule

module Second9 (
  input  set,
  input  CLK,
  output O1,
  output O2,
  output O3,
  output O4
);

  wire and_1_out;

  J_K_Flip_Flop #(.trigger("falling")) j_k_ff_1 (
    .J(set), .K(set), .clk(CLK), .Q(O1), .reset(and_1_out));  // open: Qn, preset
  LED led_1 (.in(O1));
  J_K_Flip_Flop #(.trigger("falling")) j_k_ff_2 (
    .J(set), .K(set), .clk(O1), .Q(O2), .reset(and_1_out));  // open: Qn, preset
  LED led_2 (.in(O2));
  J_K_Flip_Flop #(.trigger("falling")) j_k_ff_3 (
    .J(set), .K(set), .clk(O2), .Q(O3), .reset(and_1_out));  // open: Qn, preset
  LED led_3 (.in(O3));
  J_K_Flip_Flop #(.trigger("falling")) j_k_ff_4 (
    .J(set), .K(set), .clk(O3), .Q(O4), .reset(and_1_out));  // open: Qn, preset
  and and_1 (and_1_out, O2, O4);
  LED led_4 (.in(O4));
endmodule

module start (
  input  StartStop,
  input  Split,
  input  Reset,
  input  CLK,
  output OStartStop,
  output OSplit,
  output OReset,
  output OCLK
);

  T_Flip_Flop t_ff_1 (.T(StartStop), .clk(StartStop), .Q(OStartStop));  // open: Qn, reset, preset
  T_Flip_Flop t_ff_2 (.T(Reset), .clk(Reset), .Q(OReset));  // open: Qn, reset, preset

  assign OCLK = CLK;
  assign OSplit = Split;
endmodule
