// Logisim project Stage3.circ as structural Verilog: 4 circuits, main circuit main
module main (
);

  wire button_1_out, button_2_out, button_3_out, clock_1_out, second9_1_clock, start_1_oclk, start_1_oreset,
       start_1_ostartstop;
  wire [2:0] second5_1_o1;
  wire [3:0] second9_1_o1;

  Button button_1 (.out(button_1_out));
  Clock clock_1 (.out(clock_1_out));
  Button button_2 (.out(button_2_out));
  Hex_Digit_Display hex_digit_display_1 ();  // open: value, dp
  Hex_Digit_Display hex_digit_display_2 ();  // open: value, dp
  Button button_3 (.out(button_3_out));
  Hex_Digit_Display hex_digit_display_3 (.value({1'b0, second5_1_o1}));  // open: dp
  Second5 second5_1 (
    .reset(start_1_oreset), .set(start_1_ostartstop), .clock(second9_1_clock), .O1(second5_1_o1[0]),
    .O2(second5_1_o1[1]), .O3(second5_1_o1[2]));  // open: CLK
  LED led_1 (.in(start_1_ostartstop));
  Hex_Digit_Display hex_digit_display_4 (.value(second9_1_o1));  // open: dp
  Second9 second9_1 (
    .Reset(start_1_oreset), .set(start_1_ostartstop), .CLK(start_1_oclk), .O1(second9_1_o1[0]),
    .O2(second9_1_o1[1]), .O3(second9_1_o1[2]), .O4(second9_1_o1[3]), .Clock(second9_1_clock));
  Hex_Digit_Display hex_digit_display_5 ();  // open: value, dp
  Hex_Digit_Display hex_digit_display_6 ();  // open: value, dp
  start start_1 (
    .StartStop(button_1_out), .Split(button_2_out), .Reset(button_3_out), .CLK(clock_1_out),
    .OStartStop(start_1_ostartstop), .OReset(start_1_oreset), .OCLK(start_1_oclk));  // open: OSplit
  Hex_Digit_Display hex_digit_display_7 ();  // open: value, dp
  Hex_Digit_Display hex_digit_display_8 ();  // open: value, dp

  // Notes on the sheet:
  //   Start / Stop
  //   Stopwatch Interface
  //   Split
  //   Minutes
  //   Reset
  //   Elapsed Time
  //   Seconds
  //   :
  //   Clock Started
  //   Minutes
  //   Split Time
  //   Seconds
  //   :
endmodule

module Second9 (
  input  Reset,
  input  set,
  input  CLK,
  output O1,
  output O2,
  output O3,
  output O4,
  output Clock
);

  wire and_2_out, or_1_out;

  J_K_Flip_Flop #(.trigger("falling")) j_k_ff_1 (
    .J(set), .K(set), .clk(CLK), .Q(O1), .reset(or_1_out));  // open: Qn, preset
  LED led_1 (.in(O1));
  J_K_Flip_Flop #(.trigger("falling")) j_k_ff_2 (
    .J(set), .K(set), .clk(O1), .Q(O2), .reset(or_1_out));  // open: Qn, preset
  LED led_2 (.in(O2));
  J_K_Flip_Flop #(.trigger("falling")) j_k_ff_3 (
    .J(set), .K(set), .clk(O2), .Q(O3), .reset(or_1_out));  // open: Qn, preset
  and and_1 (Clock, O1, O4);
  LED led_3 (.in(O3));
  J_K_Flip_Flop #(.trigger("falling")) j_k_ff_4 (
    .J(set), .K(set), .clk(O3), .Q(O4), .reset(or_1_out));  // open: Qn, preset
  and and_2 (and_2_out, O2, O4);
  LED led_4 (.in(O4));
  or or_1 (or_1_out, and_2_out, Reset);
endmodule

module Second5 (
  input  reset,
  input  set,
  input  clock,
  output O1,
  output O2,
  output O3,
  output CLK
);

  wire and_2_out, or_1_out;

  J_K_Flip_Flop #(.trigger("falling")) j_k_ff_1 (
    .J(set), .K(set), .clk(clock), .Q(O1), .reset(or_1_out));  // open: Qn, preset
  LED led_1 (.in(O1));
  J_K_Flip_Flop #(.trigger("falling")) j_k_ff_2 (
    .J(set), .K(set), .clk(O1), .Q(O2), .reset(or_1_out));  // open: Qn, preset
  LED led_2 (.in(O2));
  J_K_Flip_Flop #(.trigger("falling")) j_k_ff_3 (
    .J(set), .K(set), .clk(O2), .Q(O3), .reset(or_1_out));  // open: Qn, preset
  and and_1 (CLK, O1, O3);
  LED led_3 (.in(O3));
  and and_2 (and_2_out, O2, O3);
  or or_1 (or_1_out, and_2_out, reset);
endmodule

module start (
  input  StartStop,
  input  Split,
  input  Reset,
  input  CLK,
  output OStartStop,
  output OSplit,
  output OReset,
  output OCLK
);

  T_Flip_Flop t_ff_1 (.T(StartStop), .clk(StartStop), .Q(OStartStop));  // open: Qn, reset, preset
  T_Flip_Flop t_ff_2 (.T(Reset), .clk(Reset), .Q(OReset));  // open: Qn, reset, preset

  assign OCLK = CLK;
  assign OSplit = Split;
endmodule
