// Logisim project Stage4.circ as structural Verilog: 6 circuits, main circuit main
module main (
);

  wire button_1_out, button_2_out, button_3_out, clock_1_out, minute9_1_clock, second5_1_clk,
       second9_1_clock, start_1_oclk, start_1_oreset, start_1_osplit, start_1_ostartstop;
  wire [2:0] second5_1_o1;
  wire [3:0] minute9_1_o1, minute9_2_1_o1, second9_1_o1;

  Minute9_2 minute9_2_1 (
    .Reset(start_1_oreset), .Set(start_1_ostartstop), .CLK(minute9_1_clock), .O1(minute9_2_1_o1[0]),
    .O2(minute9_2_1_o1[1]), .O3(minute9_2_1_o1[2]), .O4(minute9_2_1_o1[3]));
  Button button_1 (.out(button_1_out));
  Clock clock_1 (.out(clock_1_out));
  Button button_2 (.out(button_2_out));
  Hex_Digit_Display hex_digit_display_1 (.value(minute9_2_1_o1));  // open: dp
  Minute9 minute9_1 (
    .Reset(start_1_oreset), .Set(start_1_ostartstop), .CLK(second5_1_clk), .O1(minute9_1_o1[0]),
    .O2(minute9_1_o1[1]), .O3(minute9_1_o1[2]), .O4(minute9_1_o1[3]), .Clock(minute9_1_clock));
  Button button_3 (.out(button_3_out));
  Hex_Digit_Display hex_digit_display_2 (.value(minute9_1_o1));  // open: dp
  Hex_Digit_Display hex_digit_display_3 (.value({1'b0, second5_1_o1}));  // open: dp
  Second5 second5_1 (
    .Reset(start_1_oreset), .Set(start_1_ostartstop), .Clock(second9_1_clock), .O1(second5_1_o1[0]),
    .O2(second5_1_o1[1]), .O3(second5_1_o1[2]), .CLK(second5_1_clk));
  LED led_1 (.in(start_1_ostartstop));
  Hex_Digit_Display hex_digit_display_4 (.value(second9_1_o1));  // open: dp
  Second9 second9_1 (
    .Reset(start_1_oreset), .Set(start_1_ostartstop), .CLK(start_1_oclk), .O1(second9_1_o1[0]),
    .O2(second9_1_o1[1]), .O3(second9_1_o1[2]), .O4(second9_1_o1[3]), .Clock(second9_1_clock));
  Hex_Digit_Display hex_digit_display_5 ();  // open: value, dp
  Hex_Digit_Display hex_digit_display_6 ();  // open: value, dp
  Hex_Digit_Display hex_digit_display_7 ();  // open: value, dp
  start start_1 (
    .StartStop(button_1_out), .Split(button_2_out), .Reset(button_3_out), .CLK(clock_1_out),
    .OStartStop(start_1_ostartstop), .OSplit(start_1_osplit), .OReset(start_1_oreset), .OCLK(start_1_oclk));
  Hex_Digit_Display hex_digit_display_8 ();  // open: value, dp

  // Notes on the sheet:
  //   Start / Stop
  //   Stopwatch Interface
  //   Split
  //   Minutes
  //   Reset
  //   Elapsed Time
  //   :
  //   Clock Started
  //   Seconds
  //   Minutes
  //   Split Time
  //   :
  //   Seconds
endmodule

module Second9 (
  input  Reset,
  input  Set,
  input  CLK,
  output O1,
  output O2,
  output O3,
  output O4,
  output Clock
);

  wire and_1_out, and_2_out, and_3_out, and_4_out, or_1_out;

  J_K_Flip_Flop j_k_ff_1 (.J(Set), .K(Set), .clk(CLK), .Q(O1), .reset(or_1_out));  // open: Qn, preset
  LED led_1 (.in(O1));
  J_K_Flip_Flop j_k_ff_2 (.J(O1), .K(O1), .clk(CLK), .Q(O2), .reset(or_1_out));  // open: Qn, preset
  LED led_2 (.in(O2));
  and and_1 (and_1_out, O1, O2);
  J_K_Flip_Flop j_k_ff_3 (.J(and_1_out), .K(and_1_out), .clk(CLK), .Q(O3), .reset(or_1_out));  // open: Qn, preset
  LED led_3 (.in(O3));
  and and_2 (and_2_out, O1, O4);
  D_Flip_Flop d_ff_1 (.D(and_2_out), .clk(CLK), .Q(Clock));  // open: Qn, preset, reset
  and and_3 (and_3_out, and_1_out, O3);
  J_K_Flip_Flop j_k_ff_4 (.J(and_3_out), .K(and_3_out), .clk(CLK), .Q(O4), .reset(or_1_out));  // open: Qn, preset
  LED led_4 (.in(O4));
  or or_1 (or_1_out, and_4_out, Reset);
  and and_4 (and_4_out, O2, O4);
endmodule

module Second5 (
  input  Reset,
  input  Set,
  input  Clock,
  output O1,
  output O2,
  output O3,
  output CLK
);

  wire and_1_out, and_2_out, and_3_out, or_1_out;

  J_K_Flip_Flop j_k_ff_1 (.J(Set), .K(Set), .clk(Clock), .Q(O1), .reset(or_1_out));  // open: Qn, preset
  LED led_1 (.in(O1));
  J_K_Flip_Flop j_k_ff_2 (.J(O1), .K(O1), .clk(Clock), .Q(O2), .reset(or_1_out));  // open: Qn, preset
  LED led_2 (.in(O2));
  and and_1 (and_1_out, O1, O3);
  and and_2 (and_2_out, O1, O2);
  J_K_Flip_Flop j_k_ff_3 (.J(and_2_out), .K(and_2_out), .clk(Clock), .Q(O3), .reset(or_1_out));  // open: Qn, preset
  D_Flip_Flop d_ff_1 (.D(and_1_out), .clk(Clock), .Q(CLK));  // open: Qn, preset, reset
  LED led_3 (.in(O3));
  and and_3 (and_3_out, O2, O3);
  or or_1 (or_1_out, and_3_out, Reset);
endmodule

module Minute9 (
  input  Reset,
  input  Set,
  input  CLK,
  output O1,
  output O2,
  output O3,
  output O4,
  output Clock
);

  wire and_1_out, and_2_out, and_3_out, and_4_out, or_1_out;

  J_K_Flip_Flop j_k_ff_1 (.J(Set), .K(Set), .clk(CLK), .Q(O1), .reset(or_1_out));  // open: Qn, preset
  LED led_1 (.in(O1));
  J_K_Flip_Flop j_k_ff_2 (.J(O1), .K(O1), .clk(CLK), .Q(O2), .reset(or_1_out));  // open: Qn, preset
  LED led_2 (.in(O2));
  and and_1 (and_1_out, O1, O2);
  J_K_Flip_Flop j_k_ff_3 (.J(and_1_out), .K(and_1_out), .clk(CLK), .Q(O3), .reset(or_1_out));  // open: Qn, preset
  LED led_3 (.in(O3));
  and and_2 (and_2_out, O1, O4);
  D_Flip_Flop d_ff_1 (.D(and_2_out), .clk(CLK), .Q(Clock));  // open: Qn, preset, reset
  and and_3 (and_3_out, and_1_out, O3);
  J_K_Flip_Flop j_k_ff_4 (.J(and_3_out), .K(and_3_out), .clk(CLK), .Q(O4), .reset(or_1_out));  // open: Qn, preset
  LED led_4 (.in(O4));
  or or_1 (or_1_out, and_4_out, Reset);
  and and_4 (and_4_out, O2, O4);
endmodule

module start (
  input  StartStop,
  input  Split,
  input  Reset,
  input  CLK,
  output OStartStop,
  output OSplit,
  output OReset,
  output OCLK
);

  T_Flip_Flop t_ff_1 (.T(StartStop), .clk(StartStop), .Q(OStartStop));  // open: Qn, reset, preset
  T_Flip_Flop t_ff_2 (.T(Reset), .clk(Reset), .Q(OReset));  // open: Qn, reset, preset

  assign OCLK = CLK;
  assign OSplit = Split;
endmodule

module Minute9_2 (
  input  Reset,
  input  Set,
  input  CLK,
  output O1,
  output O2,
  output O3,
  output O4
);

  wire and_1_out, and_2_out, and_3_out, or_1_out;

  J_K_Flip_Flop j_k_ff_1 (.J(Set), .K(Set), .clk(CLK), .Q(O1), .reset(or_1_out));  // open: Qn, preset
  LED led_1 (.in(O1));
  J_K_Flip_Flop j_k_ff_2 (.J(O1), .K(O1), .clk(CLK), .Q(O2), .reset(or_1_out));  // open: Qn, preset
  LED led_2 (.in(O2));
  and and_1 (and_1_out, O1, O2);
  J_K_Flip_Flop j_k_ff_3 (.J(and_1_out), .K(and_1_out), .clk(CLK), .Q(O3), .reset(or_1_out));  // open: Qn, preset
  LED led_3 (.in(O3));
  and and_2 (and_2_out, and_1_out, O3);
  J_K_Flip_Flop j_k_ff_4 (.J(and_2_out), .K(and_2_out), .clk(CLK), .Q(O4), .reset(or_1_out));  // open: Qn, preset
  LED led_4 (.in(O4));
  or or_1 (or_1_out, and_3_out, Reset);
  and and_3 (and_3_out, O2, O4);
endmodule
