// Logisim project Stage5.circ as structural Verilog: 7 circuits, main circuit main
module main (
);

  wire button_1_out, button_2_out, button_3_out, clock_1_out, minute9_2_clock, second5_1_clk, second9_1_oclk,
       start_1_oclk, start_1_oreset, start_1_osplitstart, start_1_ostartstop;
  wire [3:0] minute9_1_o, minute9_2_o, second5_1_o, second9_1_o, stacks_1_m9_2_o, stacks_1_m9_o,
       stacks_1_s5_o, stacks_1_s9_o;

  Minute9 minute9_1 (
    .Reset(start_1_oreset), .Set(start_1_ostartstop), .CLK(minute9_2_clock), .O(minute9_1_o));  // open: Clock
  Button button_1 (.out(button_1_out));
  Clock clock_1 (.out(clock_1_out));
  Button button_2 (.out(button_2_out));
  Hex_Digit_Display hex_digit_display_1 (.value(minute9_1_o));  // open: dp
  Minute9 minute9_2 (
    .Reset(start_1_oreset), .Set(start_1_ostartstop), .CLK(second5_1_clk), .O(minute9_2_o),
    .Clock(minute9_2_clock));
  Button button_3 (.out(button_3_out));
  Hex_Digit_Display hex_digit_display_2 (.value(minute9_2_o));  // open: dp
  Hex_Digit_Display hex_digit_display_3 (.value(second5_1_o));  // open: dp
  Second5 second5_1 (
    .Reset(start_1_oreset), .Set(start_1_ostartstop), .Clock(second9_1_oclk), .O(second5_1_o),
    .CLK(second5_1_clk));
  LED led_1 (.in(start_1_ostartstop));
  Hex_Digit_Display hex_digit_display_4 (.value(second9_1_o));  // open: dp
  Second9 second9_1 (
    .Reset(start_1_oreset), .Set(start_1_ostartstop), .Clk(start_1_oclk), .O(second9_1_o),
    .OClk(second9_1_oclk));
  start start_1 (
    .StartStop(button_1_out), .Split(button_2_out), .Reset(button_3_out), .CLK(clock_1_out),
    .Ostartstop(start_1_ostartstop), .OSplitStart(start_1_osplitstart), .OReset(start_1_oreset),
    .Oclk(start_1_oclk));  // open: OSplitStop
  Stacks stacks_1 (
    .S9(second9_1_o), .S5(second5_1_o), .M9(minute9_2_o), .M9_2(minute9_1_o), .Clock(start_1_osplitstart),
    .Rst(start_1_oreset), .S9_O(stacks_1_s9_o), .S5_O(stacks_1_s5_o), .M9_O(stacks_1_m9_o),
    .M9_2_O(stacks_1_m9_2_o));
  Hex_Digit_Display hex_digit_display_5 (.value(stacks_1_m9_2_o));  // open: dp
  Hex_Digit_Display hex_digit_display_6 (.value(stacks_1_m9_o));  // open: dp
  Hex_Digit_Display hex_digit_display_7 (.value(stacks_1_s5_o));  // open: dp
  Hex_Digit_Display hex_digit_display_8 (.value(stacks_1_s9_o));  // open: dp

  // Notes on the sheet:
  //   Start / Stop
  //   Stopwatch Interface
  //   Split
  //   Minutes
  //   Reset
  //   Elapsed Time
  //   :
  //   Clock Started
  //   Seconds
  //   Minutes
  //   Split Time
  //   :
  //   Seconds
endmodule

module Second9 (
  input  Reset,
  input  Set,
  input  Clk,
  output [3:0] O,
  output OClk
);

  wire and_1_out, and_2_out, and_3_out, and_4_out, or_1_out;

  J_K_Flip_Flop j_k_ff_1 (.J(Set), .K(Set), .clk(Clk), .Q(O[0]), .reset(or_1_out));  // open: Qn, preset
  LED led_1 (.in(O[0]));
  J_K_Flip_Flop j_k_ff_2 (.J(O[0]), .K(O[0]), .clk(Clk), .Q(O[1]), .reset(or_1_out));  // open: Qn, preset
  LED led_2 (.in(O[1]));
  and and_1 (and_1_out, O[0], O[1]);
  J_K_Flip_Flop j_k_ff_3 (.J(and_1_out), .K(and_1_out), .clk(Clk), .Q(O[2]), .reset(or_1_out));  // open: Qn, preset
  LED led_3 (.in(O[2]));
  and and_2 (and_2_out, O[0], O[3]);
  D_Flip_Flop d_ff_1 (.D(and_2_out), .clk(Clk), .Q(OClk));  // open: Qn, preset, reset
  and and_3 (and_3_out, and_1_out, O[2]);
  J_K_Flip_Flop j_k_ff_4 (.J(and_3_out), .K(and_3_out), .clk(Clk), .Q(O[3]), .reset(or_1_out));  // open: Qn, preset
  LED led_4 (.in(O[3]));
  or or_1 (or_1_out, and_4_out, Reset);
  and and_4 (and_4_out, O[1], O[3]);
endmodule

module Second5 (
  input  Reset,
  input  Set,
  input  Clock,
  output [3:0] O,
  output CLK
);

  wire and_1_out, and_2_out, and_3_out, or_1_out;

  J_K_Flip_Flop j_k_ff_1 (.J(Set), .K(Set), .clk(Clock), .Q(O[0]), .reset(or_1_out));  // open: Qn, preset
  LED led_1 (.in(O[0]));
  J_K_Flip_Flop j_k_ff_2 (.J(O[0]), .K(O[0]), .clk(Clock), .Q(O[1]), .reset(or_1_out));  // open: Qn, preset
  LED led_2 (.in(O[1]));
  and and_1 (and_1_out, O[0], O[2]);
  and and_2 (and_2_out, O[0], O[1]);
  J_K_Flip_Flop j_k_ff_3 (.J(and_2_out), .K(and_2_out), .clk(Clock), .Q(O[2]), .reset(or_1_out));  // open: Qn, preset
  D_Flip_Flop d_ff_1 (.D(and_1_out), .clk(Clock), .Q(CLK));  // open: Qn, preset, reset
  LED led_3 (.in(O[2]));
  and and_3 (and_3_out, O[1], O[2]);
  or or_1 (or_1_out, and_3_out, Reset);

  assign O[3] = 1'b0;
endmodule

module Minute9 (
  input  Reset,
  input  Set,
  input  CLK,
  output [3:0] O,
  output Clock
);

  wire and_1_out, and_2_out, and_3_out, and_4_out, or_1_out;

  J_K_Flip_Flop j_k_ff_1 (.J(Set), .K(Set), .clk(CLK), .Q(O[0]), .reset(or_1_out));  // open: Qn, preset
  LED led_1 (.in(O[0]));
  J_K_Flip_Flop j_k_ff_2 (.J(O[0]), .K(O[0]), .clk(CLK), .Q(O[1]), .reset(or_1_out));  // open: Qn, preset
  LED led_2 (.in(O[1]));
  and and_1 (and_1_out, O[0], O[1]);
  J_K_Flip_Flop j_k_ff_3 (.J(and_1_out), .K(and_1_out), .clk(CLK), .Q(O[2]), .reset(or_1_out));  // open: Qn, preset
  LED led_3 (.in(O[2]));
  and and_2 (and_2_out, O[0], O[3]);
  D_Flip_Flop d_ff_1 (.D(and_2_out), .clk(CLK), .Q(Clock));  // open: Qn, preset, reset
  and and_3 (and_3_out, and_1_out, O[2]);
  J_K_Flip_Flop j_k_ff_4 (.J(and_3_out), .K(and_3_out), .clk(CLK), .Q(O[3]), .reset(or_1_out));  // open: Qn, preset
  LED led_4 (.in(O[3]));
  or or_1 (or_1_out, and_4_out, Reset);
  and and_4 (and_4_out, O[1], O[3]);
endmodule

module start (
  input  StartStop,
  input  Split,
  input  Reset,
  input  CLK,
  output Ostartstop,
  output OSplitStart,
  output OReset,
  output Oclk,
  output OSplitStop
);

  wire not_1_out, t_ff_1_q;

  T_Flip_Flop t_ff_1 (.T(StartStop), .clk(StartStop), .Q(t_ff_1_q));  // open: Qn, reset, preset
  T_Flip_Flop t_ff_2 (.T(Reset), .clk(Reset), .Q(OReset));  // open: Qn, reset, preset
  not not_1 (not_1_out, OReset);
  and and_1 (Ostartstop, t_ff_1_q, not_1_out);
  and and_2 (OSplitStart, Split, t_ff_1_q);

  assign Oclk = CLK;
  assign OSplitStop = Split;
endmodule

module Parallel (
  input  [3:0] D,
  input  Clk,
  input  Reset,
  output [3:0] O
);

  wire and_1_out, and_2_out, and_3_out, and_4_out, and_5_out;

  and and_1 (and_1_out, 1'b1, Clk);
  and and_2 (and_2_out, 1'b1, D[0]);
  D_Flip_Flop d_ff_1 (.D(and_2_out), .clk(and_1_out), .Q(O[0]), .reset(Reset));  // open: Qn, preset
  and and_3 (and_3_out, 1'b1, D[1]);
  D_Flip_Flop d_ff_2 (.D(and_3_out), .clk(and_1_out), .Q(O[1]), .reset(Reset));  // open: Qn, preset
  and and_4 (and_4_out, 1'b1, D[2]);
  D_Flip_Flop d_ff_3 (.D(and_4_out), .clk(and_1_out), .Q(O[2]), .reset(Reset));  // open: Qn, preset
  and and_5 (and_5_out, 1'b1, D[3]);
  D_Flip_Flop d_ff_4 (.D(and_5_out), .clk(and_1_out), .Q(O[3]), .reset(Reset));  // open: Qn, preset
endmodule

module Stacks (
  input  [3:0] S9,
  input  [3:0] S5,
  input  [3:0] M9,
  input  [3:0] M9_2,
  input  Clock,
  input  Rst,
  output [3:0] S9_O,
  output [3:0] S5_O,
  output [3:0] M9_O,
  output [3:0] M9_2_O
);

  Parallel parallel_1 (.D(S9), .Clk(Clock), .Reset(Rst), .O(S9_O));
  Parallel parallel_2 (.D(S5), .Clk(Clock), .Reset(Rst), .O(S5_O));
  Parallel parallel_3 (.D(M9), .Clk(Clock), .Reset(Rst), .O(M9_O));
  Parallel parallel_4 (.D(M9_2), .Clk(Clock), .Reset(Rst), .O(M9_2_O));
endmodule
