// Logisim project Stage6.circ as structural Verilog: 11 circuits, main circuit main
module main (
);

  wire button_1_out, button_2_out, button_3_out, clock_1_out, minute9_2_oclk, not_1_out, second5_1_oclk,
       second9_1_oclk, start_1_oclk, start_1_oreset, start_1_osplitstart, start_1_osplitstop,
       start_1_ostartstop;
  wire [3:0] history_1_m9_2_o, history_1_m9_o, history_1_s5_o, history_1_s9_o, minute9_1_o, minute9_2_o,
       second5_1_o, second9_1_o;

  Minute9 minute9_1 (
    .Reset(start_1_oreset), .Set(start_1_ostartstop), .CLK(minute9_2_oclk), .O(minute9_1_o));  // open: OCLK
  Button button_1 (.out(button_1_out));
  Clock clock_1 (.out(clock_1_out));
  Button button_2 (.out(button_2_out));
  Hex_Digit_Display hex_digit_display_1 (.value(minute9_1_o));  // open: dp
  Minute9 minute9_2 (
    .Reset(start_1_oreset), .Set(start_1_ostartstop), .CLK(second5_1_oclk), .O(minute9_2_o),
    .OCLK(minute9_2_oclk));
  Button button_3 (.out(button_3_out));
  Hex_Digit_Display hex_digit_display_2 (.value(minute9_2_o));  // open: dp
  Hex_Digit_Display hex_digit_display_3 (.value(second5_1_o));  // open: dp
  Second5 second5_1 (
    .Reset(start_1_oreset), .Set(start_1_ostartstop), .Clock(second9_1_oclk), .O(second5_1_o),
    .OCLK(second5_1_oclk));
  LED led_1 (.in(start_1_ostartstop));
  Hex_Digit_Display hex_digit_display_4 (.value(second9_1_o));  // open: dp
  Second9 second9_1 (
    .Reset(start_1_oreset), .Set(start_1_ostartstop), .Clk(start_1_oclk), .O(second9_1_o),
    .OClk(second9_1_oclk));
  start start_1 (
    .StartStop(button_1_out), .Split(button_2_out), .Reset(button_3_out), .CLK(clock_1_out),
    .Ostartstop(start_1_ostartstop), .OSplitStart(start_1_osplitstart), .OReset(start_1_oreset),
    .Oclk(start_1_oclk), .OSplitStop(start_1_osplitstop));
  not not_1 (not_1_out, start_1_ostartstop);
  History history_1 (
    .S9(second9_1_o), .S5(second5_1_o), .M9(minute9_2_o), .M9_2(minute9_1_o), .Clock(start_1_osplitstart),
    .Reset(start_1_oreset), .Stopped(not_1_out), .Split(start_1_osplitstop), .S9_O(history_1_s9_o),
    .S5_O(history_1_s5_o), .M9_O(history_1_m9_o), .M9_2_O(history_1_m9_2_o));
  Hex_Digit_Display hex_digit_display_5 (.value(history_1_m9_2_o));  // open: dp
  Hex_Digit_Display hex_digit_display_6 (.value(history_1_m9_o));  // open: dp
  Hex_Digit_Display hex_digit_display_7 (.value(history_1_s5_o));  // open: dp
  Hex_Digit_Display hex_digit_display_8 (.value(history_1_s9_o));  // open: dp

  // Notes on the sheet:
  //   Start / Stop
  //   Stopwatch Interface
  //   Split
  //   Minutes
  //   Reset
  //   Elapsed Time
  //   :
  //   Clock Started
  //   Seconds
  //   Minutes
  //   Split Time
  //   :
  //   Seconds
endmodule

module Second9 (
  input  Reset,
  input  Set,
  input  Clk,
  output [3:0] O,
  output OClk
);

  wire and_1_out, and_2_out, and_3_out, and_4_out, or_1_out;

  J_K_Flip_Flop j_k_ff_1 (.J(Set), .K(Set), .clk(Clk), .Q(O[0]), .reset(or_1_out));  // open: Qn, preset
  LED led_1 (.in(O[0]));
  J_K_Flip_Flop j_k_ff_2 (.J(O[0]), .K(O[0]), .clk(Clk), .Q(O[1]), .reset(or_1_out));  // open: Qn, preset
  LED led_2 (.in(O[1]));
  and and_1 (and_1_out, O[0], O[1]);
  J_K_Flip_Flop j_k_ff_3 (.J(and_1_out), .K(and_1_out), .clk(Clk), .Q(O[2]), .reset(or_1_out));  // open: Qn, preset
  LED led_3 (.in(O[2]));
  and and_2 (and_2_out, O[0], O[3]);
  D_Flip_Flop d_ff_1 (.D(and_2_out), .clk(Clk), .Q(OClk));  // open: Qn, preset, reset
  and and_3 (and_3_out, and_1_out, O[2]);
  J_K_Flip_Flop j_k_ff_4 (.J(and_3_out), .K(and_3_out), .clk(Clk), .Q(O[3]), .reset(or_1_out));  // open: Qn, preset
  LED led_4 (.in(O[3]));
  or or_1 (or_1_out, and_4_out, Reset);
  and and_4 (and_4_out, O[1], O[3]);
endmodule

module Second5 (
  input  Reset,
  input  Set,
  input  Clock,
  output [3:0] O,
  output OCLK
);

  wire and_1_out, and_2_out, and_3_out, or_1_out;

  J_K_Flip_Flop j_k_ff_1 (.J(Set), .K(Set), .clk(Clock), .Q(O[0]), .reset(or_1_out));  // open: Qn, preset
  LED led_1 (.in(O[0]));
  J_K_Flip_Flop j_k_ff_2 (.J(O[0]), .K(O[0]), .clk(Clock), .Q(O[1]), .reset(or_1_out));  // open: Qn, preset
  LED led_2 (.in(O[1]));
  and and_1 (and_1_out, O[0], O[2]);
  and and_2 (and_2_out, O[0], O[1]);
  J_K_Flip_Flop j_k_ff_3 (.J(and_2_out), .K(and_2_out), .clk(Clock), .Q(O[2]), .reset(or_1_out));  // open: Qn, preset
  D_Flip_Flop d_ff_1 (.D(and_1_out), .clk(Clock), .Q(OCLK));  // open: Qn, preset, reset
  LED led_3 (.in(O[2]));
  and and_3 (and_3_out, O[1], O[2]);
  or or_1 (or_1_out, and_3_out, Reset);

  assign O[3] = 1'b0;
endmodule

module Minute9 (
  input  Reset,
  input  Set,
  input  CLK,
  output [3:0] O,
  output OCLK
);

  wire and_1_out, and_2_out, and_3_out, and_4_out, or_1_out;

  J_K_Flip_Flop j_k_ff_1 (.J(Set), .K(Set), .clk(CLK), .Q(O[0]), .reset(or_1_out));  // open: Qn, preset
  LED led_1 (.in(O[0]));
  J_K_Flip_Flop j_k_ff_2 (.J(O[0]), .K(O[0]), .clk(CLK), .Q(O[1]), .reset(or_1_out));  // open: Qn, preset
  LED led_2 (.in(O[1]));
  and and_1 (and_1_out, O[0], O[1]);
  J_K_Flip_Flop j_k_ff_3 (.J(and_1_out), .K(and_1_out), .clk(CLK), .Q(O[2]), .reset(or_1_out));  // open: Qn, preset
  LED led_3 (.in(O[2]));
  and and_2 (and_2_out, O[0], O[3]);
  D_Flip_Flop d_ff_1 (.D(and_2_out), .clk(CLK), .Q(OCLK));  // open: Qn, preset, reset
  and and_3 (and_3_out, and_1_out, O[2]);
  J_K_Flip_Flop j_k_ff_4 (.J(and_3_out), .K(and_3_out), .clk(CLK), .Q(O[3]), .reset(or_1_out));  // open: Qn, preset
  LED led_4 (.in(O[3]));
  or or_1 (or_1_out, and_4_out, Reset);
  and and_4 (and_4_out, O[1], O[3]);
endmodule

module start (
  input  StartStop,
  input  Split,
  input  Reset,
  input  CLK,
  output Ostartstop,
  output OSplitStart,
  output OReset,
  output Oclk,
  output OSplitStop
);

  wire not_1_out, t_ff_1_q;

  T_Flip_Flop t_ff_1 (.T(StartStop), .clk(StartStop), .Q(t_ff_1_q));  // open: Qn, reset, preset
  T_Flip_Flop t_ff_2 (.T(Reset), .clk(Reset), .Q(OReset));  // open: Qn, reset, preset
  not not_1 (not_1_out, OReset);
  and and_1 (Ostartstop, t_ff_1_q, not_1_out);
  and and_2 (OSplitStart, Split, t_ff_1_q);

  assign Oclk = CLK;
  assign OSplitStop = Split;
endmodule

module Parallel (
  input  [3:0] D,
  input  Clk,
  input  Reset,
  output [3:0] O
);

  wire and_1_out, and_2_out, and_3_out, and_4_out, and_5_out;

  and and_1 (and_1_out, 1'b1, Clk);
  and and_2 (and_2_out, 1'b1, D[0]);
  D_Flip_Flop d_ff_1 (.D(and_2_out), .clk(and_1_out), .Q(O[0]), .reset(Reset));  // open: Qn, preset
  and and_3 (and_3_out, 1'b1, D[1]);
  D_Flip_Flop d_ff_2 (.D(and_3_out), .clk(and_1_out), .Q(O[1]), .reset(Reset));  // open: Qn, preset
  and and_4 (and_4_out, 1'b1, D[2]);
  D_Flip_Flop d_ff_3 (.D(and_4_out), .clk(and_1_out), .Q(O[2]), .reset(Reset));  // open: Qn, preset
  and and_5 (and_5_out, 1'b1, D[3]);
  D_Flip_Flop d_ff_4 (.D(and_5_out), .clk(and_1_out), .Q(O[3]), .reset(Reset));  // open: Qn, preset
endmodule

module Stacks (
  input  [3:0] S9,
  input  [3:0] S5,
  input  [3:0] M9,
  input  [3:0] M9_2,
  input  Clock,
  input  Reset,
  output [3:0] S9_O,
  output [3:0] S5_O,
  output [3:0] M9_O,
  output [3:0] M9_2_O
);

  Parallel parallel_1 (.D(S9), .Clk(Clock), .Reset(Reset), .O(S9_O));
  Parallel parallel_2 (.D(S5), .Clk(Clock), .Reset(Reset), .O(S5_O));
  Parallel parallel_3 (.D(M9), .Clk(Clock), .Reset(Reset), .O(M9_O));
  Parallel parallel_4 (.D(M9_2), .Clk(Clock), .Reset(Reset), .O(M9_2_O));
endmodule

module History (
  input  [3:0] S9,
  input  [3:0] S5,
  input  [3:0] M9,
  input  [3:0] M9_2,
  input  Clock,
  input  Reset,
  input  Stopped,
  input  Split,
  output [3:0] S9_O,
  output [3:0] S5_O,
  output [3:0] M9_O,
  output [3:0] M9_2_O
);

  wire demux_1_s0, demux_1_s1, demux_1_s2, demux_1_s3, demux_1_s4, not_1_out;
  wire [3:0] counter4_1_o, stacks_1_m9_2_o, stacks_1_m9_o, stacks_1_s5_o, stacks_1_s9_o, stacks_2_m9_2_o,
       stacks_2_m9_o, stacks_2_s5_o, stacks_2_s9_o, stacks_3_m9_2_o, stacks_3_m9_o, stacks_3_s5_o,
       stacks_3_s9_o, stacks_4_m9_2_o, stacks_4_m9_o, stacks_4_s5_o, stacks_4_s9_o, stacks_5_m9_2_o,
       stacks_5_m9_o, stacks_5_s5_o, stacks_5_s9_o;

  not not_1 (not_1_out, Stopped);
  Stacks stacks_1 (
    .S9(S9), .S5(S5), .M9(M9), .M9_2(M9_2), .Clock(Clock), .Reset(Reset), .S9_O(stacks_1_s9_o),
    .S5_O(stacks_1_s5_o), .M9_O(stacks_1_m9_o), .M9_2_O(stacks_1_m9_2_o));
  Hex_Digit_Display hex_digit_display_1 (.value(counter4_1_o));  // open: dp
  Counter4 counter4_1 (.Reset(not_1_out), .Set(Stopped), .Clock(Split), .O(counter4_1_o));
  LED led_1 (.in(demux_1_s0));
  Demux demux_1 (.O(counter4_1_o), .S0(demux_1_s0), .S1(demux_1_s1), .S2(demux_1_s2), .S3(demux_1_s3), .S4(demux_1_s4));
  Hex_Digit_Display hex_digit_display_2 (.value(stacks_2_m9_2_o));  // open: dp
  Hex_Digit_Display hex_digit_display_3 (.value(stacks_2_m9_o));  // open: dp
  Stacks stacks_2 (
    .S9(stacks_1_s9_o), .S5(stacks_1_s5_o), .M9(stacks_1_m9_o), .M9_2(stacks_1_m9_2_o), .Clock(Clock),
    .Reset(Reset), .S9_O(stacks_2_s9_o), .S5_O(stacks_2_s5_o), .M9_O(stacks_2_m9_o), .M9_2_O(stacks_2_m9_2_o));
  LED led_2 (.in(demux_1_s1));
  LED led_3 (.in(demux_1_s2));
  LED led_4 (.in(demux_1_s3));
  LED led_5 (.in(demux_1_s4));
  Hex_Digit_Display hex_digit_display_4 (.value(stacks_2_s5_o));  // open: dp
  Hex_Digit_Display hex_digit_display_5 (.value(stacks_2_s9_o));  // open: dp
  Hex_Digit_Display hex_digit_display_6 (.value(stacks_3_m9_2_o));  // open: dp
  Stacks stacks_3 (
    .S9(stacks_2_s9_o), .S5(stacks_2_s5_o), .M9(stacks_2_m9_o), .M9_2(stacks_2_m9_2_o), .Clock(Clock),
    .Reset(Reset), .S9_O(stacks_3_s9_o), .S5_O(stacks_3_s5_o), .M9_O(stacks_3_m9_o), .M9_2_O(stacks_3_m9_2_o));
  Hex_Digit_Display hex_digit_display_7 (.value(stacks_3_m9_o));  // open: dp
  Hex_Digit_Display hex_digit_display_8 (.value(stacks_3_s5_o));  // open: dp
  Hex_Digit_Display hex_digit_display_9 (.value(stacks_3_s9_o));  // open: dp
  Hex_Digit_Display hex_digit_display_10 (.value(stacks_4_m9_2_o));  // open: dp
  Stacks stacks_4 (
    .S9(stacks_3_s9_o), .S5(stacks_3_s5_o), .M9(stacks_3_m9_o), .M9_2(stacks_3_m9_2_o), .Clock(Clock),
    .Reset(Reset), .S9_O(stacks_4_s9_o), .S5_O(stacks_4_s5_o), .M9_O(stacks_4_m9_o), .M9_2_O(stacks_4_m9_2_o));
  Hex_Digit_Display hex_digit_display_11 (.value(stacks_4_m9_o));  // open: dp
  Hex_Digit_Display hex_digit_display_12 (.value(stacks_4_s5_o));  // open: dp
  Hex_Digit_Display hex_digit_display_13 (.value(stacks_4_s9_o));  // open: dp
  Hex_Digit_Display hex_digit_display_14 (.value(stacks_5_m9_2_o));  // open: dp
  Hex_Digit_Display hex_digit_display_15 (.value(stacks_5_m9_o));  // open: dp
  Stacks stacks_5 (
    .S9(stacks_4_s9_o), .S5(stacks_4_s5_o), .M9(stacks_4_m9_o), .M9_2(stacks_4_m9_2_o), .Clock(Clock),
    .Reset(Reset), .S9_O(stacks_5_s9_o), .S5_O(stacks_5_s5_o), .M9_O(stacks_5_m9_o), .M9_2_O(stacks_5_m9_2_o));
  Hex_Digit_Display hex_digit_display_16 (.value(stacks_5_s5_o));  // open: dp
  Hex_Digit_Display hex_digit_display_17 (.value(stacks_5_s9_o));  // open: dp
  SwitchCase switchcase_1 (
    .Stack4(stacks_5_s9_o), .Stack3(stacks_4_s9_o), .Stack2(stacks_3_s9_o), .Stack1(stacks_2_s9_o),
    .Stack0(stacks_1_s9_o), .S0(demux_1_s0), .S1(demux_1_s1), .S2(demux_1_s2), .S3(demux_1_s3),
    .S4(demux_1_s4), .out_11(S9_O));
  SwitchCase switchcase_2 (
    .Stack4(stacks_5_s5_o), .Stack3(stacks_4_s5_o), .Stack2(stacks_3_s5_o), .Stack1(stacks_2_s5_o),
    .Stack0(stacks_1_s5_o), .S0(demux_1_s0), .S1(demux_1_s1), .S2(demux_1_s2), .S3(demux_1_s3),
    .S4(demux_1_s4), .out_11(S5_O));
  SwitchCase switchcase_3 (
    .Stack4(stacks_5_m9_o), .Stack3(stacks_4_m9_o), .Stack2(stacks_3_m9_o), .Stack1(stacks_2_m9_o),
    .Stack0(stacks_1_m9_o), .S0(demux_1_s0), .S1(demux_1_s1), .S2(demux_1_s2), .S3(demux_1_s3),
    .S4(demux_1_s4), .out_11(M9_O));
  SwitchCase switchcase_4 (
    .Stack4(stacks_5_m9_2_o), .Stack3(stacks_4_m9_2_o), .Stack2(stacks_3_m9_2_o), .Stack1(stacks_2_m9_2_o),
    .Stack0(stacks_1_m9_2_o), .S0(demux_1_s0), .S1(demux_1_s1), .S2(demux_1_s2), .S3(demux_1_s3),
    .S4(demux_1_s4), .out_11(M9_2_O));

  // Notes on the sheet:
  //   Minutes
  //   Split Time
  //   :
  //   Seconds
  //   Split Time
  //   Minutes
  //   :
  //   Seconds
  //   Minutes
  //   Split Time
  //   :
  //   Seconds
  //   Minutes
  //   Split Time
  //   Seconds
  //   :
endmodule

module Counter4 (
  input  Reset,
  input  Set,
  input  Clock,
  output [3:0] O
);

  wire and_1_out, and_2_out, or_1_out;

  J_K_Flip_Flop j_k_ff_1 (.J(Set), .K(Set), .clk(Clock), .Q(O[0]), .reset(or_1_out));  // open: Qn, preset
  LED led_1 (.in(O[0]));
  J_K_Flip_Flop j_k_ff_2 (.J(O[0]), .K(O[0]), .clk(Clock), .Q(O[1]), .reset(or_1_out));  // open: Qn, preset
  LED led_2 (.in(O[1]));
  and and_1 (and_1_out, O[0], O[1]);
  J_K_Flip_Flop j_k_ff_3 (.J(and_1_out), .K(and_1_out), .clk(Clock), .Q(O[2]), .reset(or_1_out));  // open: Qn, preset
  LED led_3 (.in(O[2]));
  and and_2 (and_2_out, O[0], O[2]);
  or or_1 (or_1_out, and_2_out, Reset);

  assign O[3] = 1'b0;
endmodule

module Demux (
  input  [3:0] O,
  output S0,
  output S1,
  output S2,
  output S3,
  output S4
);

  wire buffer_1_out, buffer_2_out, buffer_3_out, not_1_out, not_2_out, not_3_out;

  not not_1 (not_1_out, O[0]);
  buf buffer_1 (buffer_1_out, O[0]);
  not not_2 (not_2_out, O[1]);
  buf buffer_2 (buffer_2_out, O[1]);
  not not_3 (not_3_out, O[2]);
  buf buffer_3 (buffer_3_out, O[2]);
  and and_1 (S0, not_1_out, not_2_out, not_3_out);
  and and_2 (S1, buffer_1_out, not_2_out, buffer_1_out);
  and and_3 (S2, not_1_out, buffer_2_out, not_3_out);
  and and_4 (S3, buffer_1_out, buffer_2_out, not_3_out);
  and and_5 (S4, not_1_out, not_2_out, buffer_3_out);
endmodule

module SwitchCase (
  input  [3:0] Stack4,
  input  [3:0] Stack3,
  input  [3:0] Stack2,
  input  [3:0] Stack1,
  input  [3:0] Stack0,
  input  S0,
  input  S1,
  input  S2,
  input  S3,
  input  S4,
  output [3:0] out_11
);

  wire and_1_out, and_2_out, and_3_out, and_4_out, and_5_out, and_6_out, and_7_out, and_8_out, and_9_out,
       and_10_out, and_11_out, and_12_out, and_13_out, and_14_out, and_15_out, and_16_out, and_17_out,
       and_18_out, and_19_out, and_20_out;

  and and_1 (and_1_out, Stack4[0], S4);
  and and_2 (and_2_out, Stack4[1], S4);
  and and_3 (and_3_out, Stack4[2], S4);
  and and_4 (and_4_out, Stack4[3], S4);
  and and_5 (and_5_out, Stack3[0], S3);
  and and_6 (and_6_out, Stack3[1], S3);
  and and_7 (and_7_out, Stack3[2], S3);
  and and_8 (and_8_out, Stack3[3], S3);
  and and_9 (and_9_out, Stack2[0], S2);
  and and_10 (and_10_out, Stack2[1], S2);
  and and_11 (and_11_out, Stack2[2], S2);
  and and_12 (and_12_out, Stack2[3], S2);
  and and_13 (and_13_out, Stack1[0], S1);
  and and_14 (and_14_out, Stack1[1], S1);
  and and_15 (and_15_out, Stack1[2], S1);
  and and_16 (and_16_out, Stack1[3], S1);
  and and_17 (and_17_out, Stack0[0], S0);
  and and_18 (and_18_out, Stack0[1], S0);
  and and_19 (and_19_out, Stack0[2], S0);
  and and_20 (and_20_out, Stack0[3], S0);
  or or_1 (out_11[0], and_1_out, and_5_out, and_9_out, and_13_out, and_17_out);
  or or_2 (out_11[1], and_2_out, and_6_out, and_10_out, and_14_out, and_18_out);
  or or_3 (out_11[2], and_3_out, and_7_out, and_11_out, and_15_out, and_19_out);
  or or_4 (out_11[3], and_4_out, and_8_out, and_12_out, and_16_out, and_20_out);
endmodule
