// Logisim project Stage1.circ as structural Verilog: 2 circuits, main circuit main
module main (
);

  wire button_1_out, button_2_out, button_3_out, clock_1_out, start_1_osplit, start_1_ostartstop;

  Hex_Digit_Display hex_digit_display_1 ();  // open: value, dp
  Hex_Digit_Display hex_digit_display_2 ();  // open: value, dp
  Button button_1 (.out(button_1_out));
  Clock clock_1 (.out(clock_1_out));
  Hex_Digit_Display hex_digit_display_3 ();  // open: value, dp
  Hex_Digit_Display hex_digit_display_4 ();  // open: value, dp
  Button button_2 (.out(button_2_out));
  Button button_3 (.out(button_3_out));
  Hex_Digit_Display hex_digit_display_5 ();  // open: value, dp
  Hex_Digit_Display hex_digit_display_6 ();  // open: value, dp
  Hex_Digit_Display hex_digit_display_7 ();  // open: value, dp
  LED led_1 (.in(start_1_ostartstop));
  Hex_Digit_Display hex_digit_display_8 ();  // open: value, dp
  start start_1 (
    .StartStop(button_1_out), .Split(button_2_out), .Reset(button_3_out), .CLK(clock_1_out),
    .OStartStop(start_1_ostartstop), .OSplit(start_1_osplit));  // open: OReset, OCLK

  // Notes on the sheet:
  //   Elapsed Time
  //   Minutes
  //   :
  //   Start / Stop
  //   Seconds
  //   Stopwatch Interface
  //   Split
  //   Reset
  //   Minutes
  //   Clock Started
  //   Split Time
  //   :
  //   Seconds
endmodule

module start (
  input  StartStop,
  input  Split,
  input  Reset,
  input  CLK,
  output OStartStop,
  output OSplit,
  output OReset,
  output OCLK
);

  T_Flip_Flop t_ff_1 (.T(StartStop), .clk(StartStop), .Q(OStartStop));  // open: Qn, reset, preset
  T_Flip_Flop t_ff_2 (.T(Reset), .clk(Reset), .Q(OReset));  // open: Qn, reset, preset

  assign OCLK = CLK;
  assign OSplit = Split;
endmodule
