// Logisim project Week1.circ as structural Verilog: 1 circuit, main circuit main
module main (
  input  in_1,
  input  in_2,
  input  in_3,
  input  in_4,
  input  in_5
);

  wire and_1_out, not_1_out, xor_1_out;

  not not_1 (not_1_out, in_1);
  and and_1 (and_1_out, in_2, in_3);
  LED led_1 (.in(not_1_out));
  LED led_2 (.in(and_1_out));
  xor xor_1 (xor_1_out, in_4, in_5);
  LED led_3 (.in(xor_1_out));
endmodule
