// Logisim project Week2.circ as structural Verilog: 3 circuits, main circuit Full_adder
module main (
  input  in_1,
  input  in_2
);

  wire and_1_out, xor_1_out;

  xor xor_1 (xor_1_out, in_1, in_2);
  LED led_1 (.in(xor_1_out));
  and and_1 (and_1_out, in_1, in_2);
  LED led_2 (.in(and_1_out));

  // Notes on the sheet:
  //   Half-adder
  //   carry output
endmodule

module Full_adder (
  input  Carry_input,
  input  in_2,
  input  in_3
);

  wire and_1_out, and_2_out, or_1_out, xor_1_out, xor_2_out;

  xor xor_1 (xor_1_out, in_2, in_3);
  and and_1 (and_1_out, in_2, in_3);
  xor xor_2 (xor_2_out, Carry_input, xor_1_out);
  and and_2 (and_2_out, Carry_input, xor_1_out);
  LED led_1 (.in(xor_2_out));
  or or_1 (or_1_out, and_2_out, and_1_out);
  LED led_2 (.in(or_1_out));

  // Notes on the sheet:
  //   Full-adder
  //   Carry output
endmodule

module four_bit (
  input  A,
  input  B,
  input  A_2,
  input  B_2,
  input  A_3,
  input  B_3,
  input  A_4,
  input  B_4
);

  wire and_1_out, and_2_out, and_3_out, and_4_out, and_5_out, and_6_out, and_7_out, or_1_out, or_2_out,
       or_3_out, xor_1_out, xor_2_out, xor_3_out, xor_4_out, xor_5_out, xor_6_out, xor_7_out;

  xor xor_1 (xor_1_out, A, B);
  and and_1 (and_1_out, A, B);
  xor xor_2 (xor_2_out, A_2, B_2);
  and and_2 (and_2_out, A_2, B_2);
  xor xor_3 (xor_3_out, A_3, B_3);
  and and_3 (and_3_out, A_3, B_3);
  xor xor_4 (xor_4_out, A_4, B_4);
  and and_4 (and_4_out, A_4, B_4);
  xor xor_5 (xor_5_out, and_1_out, xor_2_out);
  and and_5 (and_5_out, and_1_out, xor_2_out);
  xor xor_6 (xor_6_out, or_1_out, xor_3_out);
  and and_6 (and_6_out, or_1_out, xor_3_out);
  xor xor_7 (xor_7_out, or_2_out, xor_4_out);
  and and_7 (and_7_out, or_2_out, xor_4_out);
  or or_1 (or_1_out, and_5_out, and_2_out);
  or or_2 (or_2_out, and_6_out, and_3_out);
  or or_3 (or_3_out, and_7_out, and_4_out);
  LED led_1 (.in(or_3_out));
  LED led_2 (.in(xor_1_out));
  LED led_3 (.in(xor_5_out));
  LED led_4 (.in(xor_6_out));
  LED led_5 (.in(xor_7_out));

  // Notes on the sheet:
  //   S0
  //   S1
  //   S2
  //   S3
  //   Carry3
endmodule
