// Logisim project Week3.circ as structural Verilog: 4 circuits, main circuit S_R_Flipflop
module S_R_Flipflop (
  input  Set,
  input  Reset,
  input  Set_2,
  input  Reset_2
);

  wire nand_1_out, nand_2_out, nor_1_out, nor_2_out;

  nor nor_1 (nor_1_out, Set, nor_2_out);
  nor nor_2 (nor_2_out, nor_1_out, Reset);
  nand nand_1 (nand_1_out, Set_2, nand_2_out);
  nand nand_2 (nand_2_out, nand_1_out, Reset_2);
  LED led_1 (.in(nor_1_out));
  LED led_2 (.in(nor_2_out));
  LED led_3 (.in(nand_1_out));
  LED led_4 (.in(nand_2_out));

  // Notes on the sheet:
  //   Q
  //   Q'
  //   Q
  //   Q'
endmodule

module D_Flipflop (
  input  Data
);

  wire and_1_out, and_2_out, clock_1_out, d_ff_1_q, d_ff_1_qn, nor_1_out, nor_2_out, not_1_out;

  Clock clock_1 (.out(clock_1_out));
  D_Flip_Flop d_ff_1 (.D(Data), .clk(clock_1_out), .Q(d_ff_1_q), .Qn(d_ff_1_qn));  // open: preset, reset
  not not_1 (not_1_out, Data);
  LED led_1 (.in(d_ff_1_q));
  LED led_2 (.in(d_ff_1_qn));
  and and_1 (and_1_out, not_1_out, clock_1_out);
  and and_2 (and_2_out, clock_1_out, Data);
  nor nor_1 (nor_1_out, and_1_out, nor_2_out);
  nor nor_2 (nor_2_out, nor_1_out, and_2_out);
  LED led_3 (.in(nor_1_out));
  LED led_4 (.in(nor_2_out));

  // Notes on the sheet:
  //   Q
  //   Q'
endmodule

module JK_Flipflop (
  input  in_1,
  input  in_2,
  input  Set,
  input  Reset
);

  wire clock_1_out, clock_2_out, j_k_ff_1_q, j_k_ff_1_qn, nand_1_out, nand_2_out, nand_3_out, nand_4_out;

  Clock clock_1 (.out(clock_1_out));
  Clock clock_2 (.out(clock_2_out));
  J_K_Flip_Flop j_k_ff_1 (
    .J(in_1), .K(in_2), .clk(clock_1_out), .Q(j_k_ff_1_q), .Qn(j_k_ff_1_qn));  // open: preset, reset
  LED led_1 (.in(j_k_ff_1_q));
  LED led_2 (.in(j_k_ff_1_qn));
  nand nand_1 (nand_1_out, nand_4_out, Set, clock_2_out);
  nand nand_2 (nand_2_out, clock_2_out, Reset, nand_3_out);
  nand nand_3 (nand_3_out, nand_1_out, nand_4_out);
  nand nand_4 (nand_4_out, nand_3_out, nand_2_out);
  LED led_3 (.in(nand_3_out));
  LED led_4 (.in(nand_4_out));

  // Notes on the sheet:
  //   Q
  //   Q'
endmodule

module Registers (
  input  in_1,
  input  in_2,
  input  in_3,
  input  in_4,
  input  in_5
);

  wire clock_1_out, d_ff_1_q, d_ff_2_q, d_ff_3_q, d_ff_4_q;

  Clock clock_1 (.out(clock_1_out));
  D_Flip_Flop d_ff_1 (.D(in_1), .clk(clock_1_out), .Q(d_ff_1_q), .reset(in_5));  // open: Qn, preset
  LED led_1 (.in(d_ff_1_q));
  D_Flip_Flop d_ff_2 (.D(in_2), .clk(clock_1_out), .Q(d_ff_2_q), .reset(in_5));  // open: Qn, preset
  LED led_2 (.in(d_ff_2_q));
  D_Flip_Flop d_ff_3 (.D(in_3), .clk(clock_1_out), .Q(d_ff_3_q), .reset(in_5));  // open: Qn, preset
  LED led_3 (.in(d_ff_3_q));
  D_Flip_Flop d_ff_4 (.D(in_4), .clk(clock_1_out), .Q(d_ff_4_q), .reset(in_5));  // open: Qn, preset
  LED led_4 (.in(d_ff_4_q));
endmodule
