// Logisim project Week4.circ as structural Verilog
module Ripple_counter (
  input  in_1,
  input  in_2
);

  wire and_1_out, clock_1_out, clock_2_out, j_k_ff_1_q, j_k_ff_2_q, j_k_ff_3_q, j_k_ff_4_q, j_k_ff_5_q,
       j_k_ff_6_q;

  Clock clock_1 (.out(clock_1_out));
  Clock clock_2 (.out(clock_2_out));
  J_K_Flip_Flop #(.trigger("falling")) j_k_ff_1 (
    .J(in_1), .K(in_1), .clk(clock_1_out), .Q(j_k_ff_1_q));  // open: Qn, preset, reset
  J_K_Flip_Flop #(.trigger("falling")) j_k_ff_2 (
    .J(in_2), .K(in_2), .clk(clock_2_out), .Q(j_k_ff_2_q), .reset(and_1_out));  // open: Qn, preset
  // RGBLED rgbled_1: pin names not known; wires that end beside it: clock_1_out, j_k_ff_1_q
  // RGBLED rgbled_2: pin names not known; wires that end beside it: clock_2_out, j_k_ff_2_q
  J_K_Flip_Flop #(.trigger("falling")) j_k_ff_3 (
    .J(in_1), .K(in_1), .clk(j_k_ff_1_q), .Q(j_k_ff_3_q));  // open: Qn, preset, reset
  J_K_Flip_Flop #(.trigger("falling")) j_k_ff_4 (
    .J(in_2), .K(in_2), .clk(j_k_ff_2_q), .Q(j_k_ff_4_q), .reset(and_1_out));  // open: Qn, preset
  // RGBLED rgbled_3: pin names not known; wires that end beside it: j_k_ff_3_q
  // RGBLED rgbled_4: pin names not known; wires that end beside it: j_k_ff_4_q
  J_K_Flip_Flop #(.trigger("falling")) j_k_ff_5 (
    .J(in_1), .K(in_1), .clk(j_k_ff_3_q), .Q(j_k_ff_5_q));  // open: Qn, preset, reset
  J_K_Flip_Flop #(.trigger("falling")) j_k_ff_6 (
    .J(in_2), .K(in_2), .clk(j_k_ff_4_q), .Q(j_k_ff_6_q), .reset(and_1_out));  // open: Qn, preset
  // RGBLED rgbled_5: pin names not known; wires that end beside it: j_k_ff_3_q, j_k_ff_5_q
  // RGBLED rgbled_6: pin names not known; wires that end beside it: j_k_ff_4_q, j_k_ff_6_q
  and and_1 (and_1_out, j_k_ff_4_q, j_k_ff_6_q);
endmodule

module synchronous_clock (
  input  in_1,
  input  in_2
);

  wire and_1_out, and_2_out, clock_1_out, j_k_ff_1_q, j_k_ff_2_q, j_k_ff_3_q;
  wire [2:0] d_ff_1_q;

  Clock clock_1 (.out(clock_1_out));
  J_K_Flip_Flop j_k_ff_1 (
    .J(in_1), .K(in_1), .clk(clock_1_out), .Q(j_k_ff_1_q), .reset(and_2_out));  // open: Qn, preset
  LED led_1 (.in(j_k_ff_1_q));
  D_Flip_Flop d_ff_1 (.D(j_k_ff_1_q), .clk(clock_1_out), .Q(d_ff_1_q[0]));  // open: Qn, preset, reset
  J_K_Flip_Flop j_k_ff_2 (
    .J(j_k_ff_1_q), .K(j_k_ff_1_q), .clk(clock_1_out), .Q(j_k_ff_2_q), .reset(and_2_out));  // open: Qn, preset
  and and_1 (and_1_out, j_k_ff_1_q, j_k_ff_2_q);
  LED led_2 (.in(j_k_ff_2_q));
  D_Flip_Flop d_ff_2 (.D(j_k_ff_2_q), .clk(clock_1_out), .Q(d_ff_1_q[1]));  // open: Qn, preset, reset
  J_K_Flip_Flop j_k_ff_3 (
    .J(and_1_out), .K(and_1_out), .clk(clock_1_out), .Q(j_k_ff_3_q), .reset(and_2_out));  // open: Qn, preset
  and and_2 (and_2_out, j_k_ff_3_q, j_k_ff_2_q);
  LED led_3 (.in(j_k_ff_3_q));
  D_Flip_Flop d_ff_3 (.D(j_k_ff_3_q), .clk(clock_1_out), .Q(d_ff_1_q[2]));  // open: Qn, preset, reset
  Hex_Digit_Display hex_digit_display_1 (.value({in_2, d_ff_1_q}));  // open: dp
endmodule
